# Fritzing sketch pad (saved by Fritzing 0.9.3b)

parts:
  Part1 = Arduino Micro (Rev3)
  U1 = SLIDER [package=slider]
  U2 = SLIDER [package=slider]
  U3 = SLIDER [package=slider]
  Generic_4x4_button_keypad1 = Generic 4x4 Keypad  # not connected
  S1 = Taiway 100-SP-X-T1 SPDT Miniature Toggle Switch [part_number=100-SP-X-T1-0-0-B1-M2 package=THT]
  S2 = Taiway 100-SP-X-T1 SPDT Miniature Toggle Switch [part_number=100-SP-X-T1-0-0-B1-M2 package=THT]
  S3 = Taiway 100-SP-X-T1 SPDT Miniature Toggle Switch [part_number=100-SP-X-T1-0-0-B1-M2 package=THT]
  SW1 = ENCODER_RGB_CA [package=encoder_led_3]
  SW2 = ENCODER_RGB_CA [package=encoder_led_3]  # not connected
  SW3 = ENCODER_RGB_CA [package=encoder_led_3]  # not connected
  SW4 = ENCODER_RGB_CA [package=encoder_led_3]
  IC1 = MCP23S17 I2C I/O Expander  # not connected

nets:
  N1: Part1.GND, U1.E, U2.E, U3.E, S1.COM, S2.COM, S3.COM, SW4.C
  N2: Part1.D2/SDA, S3.L2
  N3: Part1.D3/SCL, S2.L2
  N4: Part1.D4_PWM/A6, S1.L2
  N5: Part1.5V, U1.A, U2.A, U3.A, SW1.B
  N6: Part1.A2, U3.S
  N7: Part1.A1, U2.S
  N8: Part1.A0, U1.S

custom parts:
  Generic 4x4 Keypad: generic 4x4 keypad 4 rows of four 6 mm tact switches cheap and nasty but works
  MCP23S17 I2C I/O Expander: The MCP23017 uses two i2c pins (these can be shared with other i2c devices), and in exchange gives you 16 general purpose pins. You can set each of 16 pins to be input, output, input with a pullup or open drain. There's even the ability to get an interrupt via an external pin when any of the inputs change so you don't have to keep polling the chip.
